# Fritzing sketch Schéma partie controle (saved by Fritzing 0.9.3b)
breadboards: 2

parts:
  RE1 = Rotary Encoder [package=THT]  # not connected
  R1 = Resistor [tolerance=±5% resistance=1k package=THT]
  LED1 = LED - 5mm [color="Red (633nm)" package="5 mm [THT]"]
  R2 = Resistor [tolerance=±1% resistance=330 package=THT]
  LED2 = LED - 5mm [color="Red (633nm)" package="5 mm [THT]"]
  LED3 = LED - 5mm [color="Red (633nm)" package="5 mm [THT]"]
  LED4 = LED - 5mm [color="Red (633nm)" package="5 mm [THT]"]
  LED5 = LED - 5mm [color="Red (633nm)" package="5 mm [THT]"]
  R3 = Resistor [tolerance=±1% resistance=330 package=THT]
  R4 = Resistor [tolerance=±1% resistance=330 package=THT]
  R5 = Resistor [tolerance=±1% resistance=330 package=THT]
  R6 = Resistor [tolerance=±1% resistance=330 package=THT]
  Part1 = Arduino Leonardo (Rev3b)
  Relay_5V1 = Keyes Relay [package=THT]
  Relay_5V2 = Keyes Relay [package=THT]
  Relay_5V3 = Keyes Relay [package=THT]
  Relay_5V4 = Keyes Relay [package=THT]
  R7 = Photocell (LDR) [package=THT]
  R8 = Resistor [tolerance=±5% resistance=10k package=THT]
  hc-sr1 = hc-sr04

nets:
  GND: R1.Pin_0, LED1.anode, LED2.cathode, LED3.anode, LED4.anode, LED5.cathode, Part1.GND, Relay_5V1.ground, Relay_5V2.ground, Relay_5V3.ground, Relay_5V4.ground, R8.Pin_1, hc-sr1.GND
  N1: LED1.cathode, R2.Pin_1
  N2: LED2.anode, R6.Pin_1
  N3: LED3.cathode, R3.Pin_1
  N4: LED4.cathode, R4.Pin_1
  N5: LED5.anode, R5.Pin_1
  N6: R3.Pin_0, Relay_5V3.NO
  N7: R4.Pin_0, Relay_5V2.NO
  N8: R5.Pin_0, Relay_5V4.NO
  N9: R6.Pin_0, Relay_5V1.NO
  N10: Part1.3V3, Part1.A0, R7.pin_1, R8.Pin_0
  5V: Part1.5V, Relay_5V1.power, Relay_5V2.power, Relay_5V3.power, Relay_5V4.power, hc-sr1.VCC
  N11: Part1.D8/A8, Relay_5V4.signal
  N12: Part1.D9_PWM/A9, Relay_5V1.signal
  N13: Part1.D10_PWM/A10, Relay_5V2.signal
  N14: Part1.D11_PWM, Relay_5V3.signal
  N15: Part1.D12/A11, hc-sr1.Trig
  N16: Part1.D13_PWM, hc-sr1.Echo
  N17: Relay_5V1.C, Relay_5V2.C, Relay_5V3.C, Relay_5V4.C

custom parts:
  Keyes Relay: The Keyes 5V relay module is suitable for SCM development, home appliance control. It uses a 5V~12V TIL control signal which can control DC / AC signal.
