# Fritzing sketch bluetoothLight (saved by Fritzing 0.9.3b)
circuit board: 5.95923cm x 6.3306cm
breadboards: 1

parts:
  HC-06 = Bluetooth HC-05 Macho
  Arduino_UNO = Arduino Uno (Rev3)
  Relay_5V = Keyes Relay [package=THT]
  S1 = Pushbutton [package="[THT]"]
  R1 = Resistor [tolerance=±5% resistance=10k package=THT]

nets:
  N1: HC-06.TXD, Arduino_UNO.D0/RX
  N2: HC-06.RXD, Arduino_UNO.D1/TX
  VCC: HC-06.VCC, Arduino_UNO.5V, Relay_5V.power, S1.Pin_3, S1.Pin_4
  GND: HC-06.GND, Arduino_UNO.GND, Relay_5V.ground, R1.Pin_0
  N3: Arduino_UNO.D12/MISO, S1.Pin_1, S1.Pin_2, R1.Pin_1
  N4: Arduino_UNO.D13/SCK, Relay_5V.signal
  N5: Relay_5V.NC, Relay_5V.C, Relay_5V.NO

custom parts:
  Keyes Relay: The Keyes 5V relay module is suitable for SCM development, home appliance control. It uses a 5V~12V TIL control signal which can control DC / AC signal.

// code stored in the sketch: bluetoothLight.ino
char blueToothVal;           //value sent over via bluetooth
char lastValue;              //stores last state of device (on/off)
 
void setup()
{
 Serial.begin(9600); 
 pinMode(13,OUTPUT);
 pinMode(12,INPUT);
}
 
 
void loop()
{
  if(Serial.available())
  {//if there is data being recieved
    blueToothVal=Serial.read(); //read it
  }
  if (blueToothVal=='n')
  {//if value from bluetooth serial is n
    digitalWrite(13,HIGH);            //switch on LED
    if (lastValue!='n')
      Serial.println(F("LED is on")); //print LED is on
    lastValue=blueToothVal;
  }
  else if (blueToothVal=='f')
  {//if value from bluetooth serial is n
    digitalWrite(13,LOW);             //turn off LED
    if (lastValue!='f')
      Serial.println(F("LED is off")); //print LED is on
    lastValue=blueToothVal;
  }
  delay(250);
}
